# Fritzing sketch LightUpWheelGryoV1 (saved by Fritzing 0.9.10b)
circuit board: 8.37543cm x 2.18467cm

parts:
  Part1 = Arduino Micro (Rev3)
  S1 = Pushbutton [package=THT]
  S2 = Toggle Switch [package=THT]
  GND = Pad [width=3.0357828288288324 height=1.7238400300300267 connect=center]
  A3 = Pad [width=3.0357828288288324 height=1.7238400300300267 connect=center]
  A2 = Pad [width=3.0357828288288324 height=1.7238400300300267 connect=center]
  A1 = Pad [width=3.0357828288288324 height=1.7238400300300267 connect=center]
  + = Pad [width=1.6323123123123178 height=2.4560960960960934 connect=center]
  - = Pad [width=1.6323123123123178 height=2.4560960960960934 connect=center]
  U1 = mystery part, 3 pins [chip_label=?]

nets:
  N1: Part1.GND, GND.pad, +.pad, U1.pin1
  N2: Part1.D2/SDA, U1.pin3
  N3: Part1.D7, S2.L1
  N4: Part1.D8_PWM/A8, S1.leg0
  N5: Part1.VIN, -.pad
  N6: Part1.5V, U1.pin2
  N7: Part1.A3, A3.pad
  N8: Part1.A2, A2.pad
  N9: Part1.A1, A1.pad
  N10: Part1.3V3, S1.leg1, S2.COM, S2.L2

notes:
  Team Wheel 2022
