# Fritzing sketch LightUpWheelGryoV3 (saved by Fritzing 0.9.10b)
circuit board: 10.1111cm x 2.1cm

parts:
  Part1 = Arduino Micro (Rev3)
  Part2 = InvenSense MPU6050
  U1 = ESP8266 WiFi Module [part_number=ESP8266]
  S1 = Pushbutton [package=THT]
  S2 = Toggle Switch [package=THT]
  GND = Pad [width=3.0357828288288324 height=1.7238400300300267 connect=center]
  A3 = Pad [width=3.0357828288288324 height=1.7238400300300267 connect=center]
  A2 = Pad [width=3.0357828288288324 height=1.7238400300300267 connect=center]
  A1 = Pad [width=3.0357828288288324 height=1.7238400300300267 connect=center]
  + = Pad [width=1.6323123123123178 height=2.4560960960960934 connect=center]
  - = Pad [width=1.6323123123123178 height=2.4560960960960934 connect=center]

nets:
  GND: Part1.GND, Part2.GND, U1.GND, GND.pad, +.pad
  N1: Part1.D7, S2.L1
  N2: Part1.D8_PWM/A8, S1.leg0
  N3: Part1.D10_PWM/A10, U1.TXD
  N4: Part1.D11_PWM, U1.RXD
  N5: Part1.VIN, -.pad
  5V: Part1.5V, Part2.VCC
  N6: Part1.A5, Part2.SCL
  N7: Part1.A4, Part2.SDA
  N8: Part1.A3, A3.pad
  N9: Part1.A2, A2.pad
  N10: Part1.A1, A1.pad
  3V3: Part1.3V3, U1.VCC, S1.leg1, S2.COM, S2.L2

notes:
  Team Wheel 2022
