# Fritzing sketch LightUpWheelGryoV5 (saved by Fritzing 0.9.10b)
circuit board: 11.1254cm x 2.73783cm

parts:
  Part1 = Arduino Micro (Rev3)
  A3 = Pad [width=3.0357828288288324 height=1.7238400300300267 connect=center]  # not connected
  A2 = Pad [width=3.0357828288288324 height=1.7238400300300267 connect=center]  # not connected
  A1 = Pad [width=3.0357828288288324 height=1.7238400300300267 connect=center]  # not connected
  + = Pad [width=1.6323123123123178 height=2.4560960960960934 connect=center]
  - = Pad [width=1.6323123123123178 height=2.4560960960960934 connect=center]
  GND = Pad [width=3.0357828288288324 height=1.7238400300300267 connect=center]
  VCC = Pad [width=3.0357828288288324 height=1.7238400300300267 connect=center]
  HC-05 = Bluetooth HC-05 Macho

nets:
  N1: Part1.D1/TX, HC-05.TXD
  N2: Part1.D0/RX, HC-05.RXD
  GND: Part1.GND, +.pad, GND.pad, HC-05.GND
  N3: Part1.VIN, -.pad, VCC.pad
  5V: Part1.5V, HC-05.VCC
  N4: Part1.3V3, HC-05.Key

notes:
  Team Wheel 2022
